// Logisim project ALU.circ as structural Verilog: 1 circuit, main circuit main
module main (
  input  [31:0] A,
  input  [31:0] B,
  input  [3:0] Control,
  output Zero,
  output [31:0] Out
);

  wire comparator_1_lt, decoder_1_out0, decoder_1_out1, decoder_1_out2, decoder_1_out6, decoder_1_out7,
       not_1_out;
  wire [31:0] adder_1_out, and_1_out, controlled_buffer_4_out, or_1_out, subtractor_1_out;

  Decoder #(.select(4), .enable("false")) decoder_1 (
    .out0(decoder_1_out0), .out1(decoder_1_out1), .out2(decoder_1_out2), .out6(decoder_1_out6),
    .out7(decoder_1_out7), .sel(Control));  // open: out3, out4, out5, out8, out9, out10, out11, out12, out13, out14, out15
  assign or_1_out = A | B;  // OR_Gate or_1, 32 bits wide
  assign Out = decoder_1_out0 ? and_1_out : 32'bz;  // Controlled_Buffer controlled_buffer_1
  assign and_1_out = A & B;  // AND_Gate and_1, 32 bits wide
  assign Out = decoder_1_out1 ? or_1_out : 32'bz;  // Controlled_Buffer controlled_buffer_2
  Adder #(.width(32)) adder_1 (.a(A), .b(B), .out(adder_1_out), .cin(1'b0));  // open: cout
  Subtractor #(.width(32)) subtractor_1 (.a(A), .b(B), .out(subtractor_1_out), .bin(1'b0));  // open: bout
  assign Out = decoder_1_out2 ? adder_1_out : 32'bz;  // Controlled_Buffer controlled_buffer_3
  Comparator #(.width(32)) comparator_1 (
    .a(subtractor_1_out), .b({32{1'b0}}), .eq(Zero), .lt(comparator_1_lt));  // open: gt
  not not_1 (not_1_out, comparator_1_lt);
  assign controlled_buffer_4_out = comparator_1_lt ? 32'h1 : 32'bz;  // Controlled_Buffer controlled_buffer_4
  assign Out = decoder_1_out6 ? subtractor_1_out : 32'bz;  // Controlled_Buffer controlled_buffer_5
  assign Out = decoder_1_out7 ? controlled_buffer_4_out : 32'bz;  // Controlled_Buffer controlled_buffer_6
  assign controlled_buffer_4_out = not_1_out ? {32{1'b0}} : 32'bz;  // Controlled_Buffer controlled_buffer_7

  // Notes on the sheet:
  //   0111 slt
endmodule
