// Logisim project Hazard-2.circ as structural Verilog: 17 circuits, main circuit main
module main (
  input  \连续运行 ,
  input  in_2,
  input  IEnable
);

  wire and_1_out, button_1_out, button_2_out, clock_1_out, clockgen_1_t1, clockgen_1_t2, clockgen_1_t3,
       ex_mem_1_branch, ex_mem_1_memread, ex_mem_1_memwrite, ex_mem_1_zero_out, id_ex_1_alusrc,
       id_ex_1_regdst, main_1_zero, mem_wb_1_memtoreg, mem_wb_1_regwrite, Reset_out;
  wire [1:0] controler_1_wb_out, ex_mem_1_wb_output, forwardingunit_1_forwarda, forwardingunit_1_forwardb,
       id_ex_1_wb_out;
  wire [2:0] controler_1_m_out, id_ex_1_m_out;
  wire [3:0] id_ex_1_aluop4;
  wire [4:0] ex_mem_1__5_rd_out, id_ex_1__15_11_rd_out, id_ex_1__20_16_rt_out, id_ex_1__26_21_rs_out,
       mem_wb_1__5_rd_result, multiplexer_2_out;
  wire [5:0] controler_1_ex_out, if_id_1_c_instruct, if_id_1_c_instruct_3;
  wire [25:6] if_id_1_c_instruct_2;
  wire [31:0] add_alu_1_out, add_alu_2_out, dmemory_1_dout, ex_mem_1_alu_result_out, ex_mem_1_fatch_2_out,
       ex_mem_1_new_pc_out, id_ex_1__15_0_signex_out, id_ex_1_c_pc_4_out, id_ex_1_fatch1_out,
       id_ex_1_fatch2_out, if_id_1_c_pc_4, imemory_1_iout, left_shift_1_out, main_1_out,
       mem_wb_1_alu_result_out, mem_wb_1_mem_read_out, multiplexer_1_out, multiplexer_3_out,
       multiplexer_4_out, multiplexer_5_out, multiplexer_6_out, pc_1_out, registers_32_1_output0,
       registers_32_1_output1, signextend_1_out;

  Multiplexer #(.width(32), .enable("false")) multiplexer_1 (
    .in0(add_alu_1_out), .in1(ex_mem_1_new_pc_out), .out(multiplexer_1_out), .sel(and_1_out));
  Button Reset (.out(Reset_out));
  PC pc_1 (.Input(multiplexer_1_out), .Clk(clockgen_1_t3), .Clear(Reset_out), .Out(pc_1_out));
  // Probe on pc_1_out
  ADD_ALU add_alu_1 (.A(pc_1_out), .B(32'h1), .Out(add_alu_1_out));
  IMemory imemory_1 (.IAddress(pc_1_out), .IEnable(IEnable), .IOut(imemory_1_iout));
  IF_ID if_id_1 (
    .PC_4(add_alu_1_out), .Instruct(imemory_1_iout), .C_PC_4(if_id_1_c_pc_4),
    .C_Instruct({if_id_1_c_instruct_3, if_id_1_c_instruct_2, if_id_1_c_instruct}), .Clk(clockgen_1_t3),
    .reset(Reset_out));
  // Probe on {if_id_1_c_instruct_3, if_id_1_c_instruct_2, if_id_1_c_instruct}
  Controler controler_1 (
    .Opcode(if_id_1_c_instruct_3), .Ex_out(controler_1_ex_out), .funct(if_id_1_c_instruct),
    .M_out(controler_1_m_out), .WB_out(controler_1_wb_out));
  // Probe on if_id_1_c_instruct_2[25:21]
  // Probe on if_id_1_c_instruct_2[20:16]
  Registers_32 registers_32_1 (
    .ReadReg0(if_id_1_c_instruct_2[25:21]), .ReadReg1(if_id_1_c_instruct_2[20:16]), .Reset(Reset_out),
    .RegWrite(mem_wb_1_regwrite), .WriteData(multiplexer_6_out), .Output0(registers_32_1_output0),
    .OutPut1(registers_32_1_output1), .WriteReg(mem_wb_1__5_rd_result), .T0(clockgen_1_t1), .T1(clockgen_1_t2));
  // Probe on registers_32_1_output0
  // Probe on registers_32_1_output1
  signExtend signextend_1 (.In({if_id_1_c_instruct_2[15:6], if_id_1_c_instruct}), .Out(signextend_1_out));
  ID_EX id_ex_1 (
    .WB(controler_1_wb_out), .M(controler_1_m_out), .EX(controler_1_ex_out), .C_PC_4(if_id_1_c_pc_4),
    .Fatch1(registers_32_1_output0), .Fatch2(registers_32_1_output1), ._15_0_signEx(signextend_1_out),
    ._20_16_rt(if_id_1_c_instruct_2[20:16]), ._15_11_rd(if_id_1_c_instruct_2[15:11]), .T1(clockgen_1_t3),
    .reset(Reset_out), .WB_out(id_ex_1_wb_out), .M_out(id_ex_1_m_out), .RegDst(id_ex_1_regdst),
    .ALUOp4(id_ex_1_aluop4), .ALUSrc(id_ex_1_alusrc), .C_PC_4_out(id_ex_1_c_pc_4_out),
    .Fatch1_out(id_ex_1_fatch1_out), .Fatch2_out(id_ex_1_fatch2_out),
    ._15_0_signEx_out(id_ex_1__15_0_signex_out), ._20_16_rt_out(id_ex_1__20_16_rt_out),
    ._15_11_rd_out(id_ex_1__15_11_rd_out), .T0(clockgen_1_t1), ._26_21_rs(if_id_1_c_instruct_2[25:21]),
    ._26_21_rs_out(id_ex_1__26_21_rs_out));
  left_shift left_shift_1 (.Input(id_ex_1__15_0_signex_out), .distance(5'b00010), .Out(left_shift_1_out));
  Multiplexer #(.width(5), .enable("false")) multiplexer_2 (
    .in0(id_ex_1__20_16_rt_out), .in1(id_ex_1__15_11_rd_out), .out(multiplexer_2_out), .sel(id_ex_1_regdst));
  ADD_ALU add_alu_2 (.A(id_ex_1_c_pc_4_out), .B(left_shift_1_out), .Out(add_alu_2_out));
  Multiplexer #(.select(2), .width(32), .enable("false")) multiplexer_3 (
    .in0(id_ex_1_fatch1_out), .in1(multiplexer_6_out), .in2(ex_mem_1_alu_result_out),
    .out(multiplexer_3_out), .sel(forwardingunit_1_forwarda));  // open: in3
  Multiplexer #(.width(32), .enable("false")) multiplexer_4 (
    .in0(multiplexer_5_out), .in1(id_ex_1__15_0_signex_out), .out(multiplexer_4_out), .sel(id_ex_1_alusrc));
  Multiplexer #(.select(2), .width(32), .enable("false")) multiplexer_5 (
    .in0(id_ex_1_fatch2_out), .in1(multiplexer_6_out), .in2(ex_mem_1_alu_result_out),
    .out(multiplexer_5_out), .sel(forwardingunit_1_forwardb));  // open: in3
  ALU_main main_1 (
    .A(multiplexer_3_out), .B(multiplexer_4_out), .Control(id_ex_1_aluop4), .Zero(main_1_zero),
    .Out(main_1_out));
  ForwardingUnit forwardingunit_1 (
    .EX_MEM_Rd(ex_mem_1__5_rd_out), .MEM_WB_Rd(mem_wb_1__5_rd_result), .ID_EX_Rs(id_ex_1__26_21_rs_out),
    .ID_EX_Rt(id_ex_1__20_16_rt_out), .ForwardA(forwardingunit_1_forwarda),
    .ForwardB(forwardingunit_1_forwardb), .EX_MEM_M_RegWrite(ex_mem_1_wb_output[1]),
    .MEM_WB_M_RegWrite(mem_wb_1_regwrite));
  // Probe on ex_mem_1__5_rd_out
  // Probe on mem_wb_1__5_rd_result
  EX_MEM ex_mem_1 (
    .WB(id_ex_1_wb_out), .M(id_ex_1_m_out), .New_PC(add_alu_2_out), .Zero(main_1_zero),
    .ALU_result(main_1_out), .Fatch_2(multiplexer_5_out), ._5_rd(multiplexer_2_out), .clk(clockgen_1_t1),
    .reset(Reset_out), .WB_output(ex_mem_1_wb_output), .MemWrite(ex_mem_1_memwrite),
    .MemRead(ex_mem_1_memread), .Branch(ex_mem_1_branch), .new_PC_out(ex_mem_1_new_pc_out),
    .ALU_result_out(ex_mem_1_alu_result_out), .Fatch_2_out(ex_mem_1_fatch_2_out),
    ._5_rd_out(ex_mem_1__5_rd_out), .Zero_out(ex_mem_1_zero_out));
  and and_1 (and_1_out, ex_mem_1_branch, ex_mem_1_zero_out);
  // Probe on ex_mem_1_alu_result_out
  DMemory dmemory_1 (
    .DAddress(ex_mem_1_alu_result_out), .Data(ex_mem_1_fatch_2_out), .Clk(clockgen_1_t3),
    .MemoryRead(ex_mem_1_memread), .MemoryWrite(ex_mem_1_memwrite), .Dout(dmemory_1_dout));
  MEM_WB mem_wb_1 (
    .WB(ex_mem_1_wb_output), .mem_data(dmemory_1_dout), .ALU_result(ex_mem_1_alu_result_out),
    ._5_rd(ex_mem_1__5_rd_out), .clk(clockgen_1_t3), .reset(Reset_out), .MemToReg(mem_wb_1_memtoreg),
    .RegWrite(mem_wb_1_regwrite), .mem_read_out(mem_wb_1_mem_read_out),
    .ALU_result_out(mem_wb_1_alu_result_out), ._5_rd_result(mem_wb_1__5_rd_result));
  Button button_1 (.out(button_1_out));
  Multiplexer #(.width(32), .enable("false")) multiplexer_6 (
    .in0(mem_wb_1_alu_result_out), .in1(mem_wb_1_mem_read_out), .out(multiplexer_6_out),
    .sel(mem_wb_1_memtoreg));
  Clock clock_1 (.out(clock_1_out));
  ClockGen clockgen_1 (
    .\单节拍按钮 (button_2_out), .\主频 (clock_1_out), .\单周期按钮 (button_1_out), .\单拍0_单周期1 (in_2), .\连续运行1 (\连续运行 ),
    .T3(clockgen_1_t3), .T2(clockgen_1_t2), .T1(clockgen_1_t1));  // open: T4
  Button button_2 (.out(button_2_out));

  // Notes on the sheet:
  //   单周期
  //   单节拍
endmodule

module IMemory (
  input  [31:0] IAddress,
  input  IEnable,
  output [31:0] IOut
);

  wire [15:0] bit_extender_1_out;

  Bit_Extender #(.in_width(32)) bit_extender_1 (.in(IAddress), .out(bit_extender_1_out));
  ROM #(.addrWidth(16), .dataWidth(32)) rom_1 (.addr(bit_extender_1_out), .data(IOut), .sel(IEnable));

  // Notes on the sheet:
  //   contents of rom_1 (hex, n*v repeats v):
  //   1084022 16b5822 8d0900ff 8d0a00fe 12a5820 ad0b00fd 12a5822 ad0b00fc 12a5824 ad0b00fb 12a5825
  //   ad0b00fa 18b602a 1ad6822 1ac6820 1ab702a 11ccfffd ad0d00f9
endmodule

module DMemory (
  input  [31:0] DAddress,
  input  [31:0] Data,
  input  Clk,
  input  MemoryRead,
  input  MemoryWrite,
  output [31:0] Dout
);

  wire [15:0] bit_extender_1_out;

  Bit_Extender #(.in_width(32)) bit_extender_1 (.in(DAddress), .out(bit_extender_1_out));
  RAM #(.addrWidth(16), .dataWidth(32), .bus("separate")) ram_1 (
    .addr(bit_extender_1_out), .din(Data), .data(Dout), .str(MemoryWrite), .sel(1'b1), .clk(Clk),
    .ld(MemoryRead));  // open: clr
endmodule

module ADD_ALU (
  input  [31:0] A,
  input  [31:0] B,
  output [31:0] Out
);

  Adder #(.width(32)) adder_1 (.a(A), .b(B), .out(Out), .cin(1'b0));  // open: cout
endmodule

module PC (
  input  [31:0] Input,
  input  Clear,
  input  Clk,
  output [31:0] Out
);

  Register #(.width(32)) PC (.D(Input), .en(1'b1), .Q(Out), .clk(Clk), .clr(Clear));
endmodule

module IF_ID (
  input  [31:0] PC_4,
  input  [31:0] Instruct,
  input  Clk,
  input  reset,
  output [31:0] C_PC_4,
  output [31:0] C_Instruct
);

  Register #(.width(32)) register_1 (.D(PC_4), .en(1'b1), .Q(C_PC_4), .clk(Clk), .clr(reset));
  Register #(.width(32)) register_2 (.D(Instruct), .en(1'b1), .Q(C_Instruct), .clk(Clk), .clr(reset));
endmodule

module Registers_32 (
  input  [4:0] ReadReg0,
  input  [4:0] ReadReg1,
  input  T0,
  input  T1,
  input  [4:0] WriteReg,
  input  Reset,
  input  RegWrite,
  input  [31:0] WriteData,
  output [31:0] Output0,
  output [31:0] OutPut1
);

  wire and_1_out, not_1_out, or_1_out;
  wire [4:0] multiplexer_1_out;
  wire [7:0] decoder_2_out15, decoder_2_out23, decoder_2_out31;
  wire [31:0] a0_out_7, a1_out_7, a2_out_7, a3_out_7, at_out_7, decoder_1_out31, fp_out_7, gp_out_7,
       k0_out_7, k1_out_7, ra_out_7, s0_out_7, s1_out_7, s2_out_7, s3_out_7, s4_out_7, s5_out_7, s6_out_7,
       s7_out_7, sp_out_7, t0_out_7, t1_out_7, t2_out_7, t3_out_7, t4_out_7, t5_out_7, t6_out_7, t7_out_7,
       t8_out_7, t9_out_7, v0_out_7, v1_out_7, Zero_out_7, Zero_output;
  wire [31:24] decoder_2_out7;

  not not_1 (not_1_out, T0);
  Multiplexer #(.width(5), .enable("false")) multiplexer_1 (
    .in0(ReadReg0), .in1(ReadReg1), .out(multiplexer_1_out), .sel(and_1_out));
  and and_1 (and_1_out, not_1_out, T1);
  or or_1 (or_1_out, T1, T0);
  // Probe on Zero_out_7
  // Probe on at_out_7
  // Probe on v0_out_7
  // Probe on v1_out_7
  // Probe on a0_out_7
  // Probe on a1_out_7
  // Probe on a2_out_7
  // Probe on a3_out_7
  Ri Zero (
    .Ri_B(decoder_1_out31[31]), .LDRi(1'b0), .T(or_1_out), .out_7(Zero_out_7), .OutPut(Zero_output),
    .Reset(1'b1), .Write(1'b0));  // open: Input
  Ri at (
    .Input(WriteData), .Ri_B(decoder_1_out31[30]), .LDRi(decoder_2_out7[30]), .T(or_1_out), .out_7(at_out_7),
    .OutPut(Zero_output), .Reset(Reset), .Write(RegWrite));
  Ri v0 (
    .Input(WriteData), .Ri_B(decoder_1_out31[29]), .LDRi(decoder_2_out7[29]), .T(or_1_out), .out_7(v0_out_7),
    .OutPut(Zero_output), .Reset(Reset), .Write(RegWrite));
  Ri v1 (
    .Input(WriteData), .Ri_B(decoder_1_out31[28]), .LDRi(decoder_2_out7[28]), .T(or_1_out), .out_7(v1_out_7),
    .OutPut(Zero_output), .Reset(Reset), .Write(RegWrite));
  Ri a0 (
    .Input(WriteData), .Ri_B(decoder_1_out31[27]), .LDRi(decoder_2_out7[27]), .T(or_1_out), .out_7(a0_out_7),
    .OutPut(Zero_output), .Reset(Reset), .Write(RegWrite));
  Ri a1 (
    .Input(WriteData), .Ri_B(decoder_1_out31[26]), .LDRi(decoder_2_out7[26]), .T(or_1_out), .out_7(a1_out_7),
    .OutPut(Zero_output), .Reset(Reset), .Write(RegWrite));
  Ri a2 (
    .Input(WriteData), .Ri_B(decoder_1_out31[25]), .LDRi(decoder_2_out7[25]), .T(or_1_out), .out_7(a2_out_7),
    .OutPut(Zero_output), .Reset(Reset), .Write(RegWrite));
  Ri a3 (
    .Input(WriteData), .Ri_B(decoder_1_out31[24]), .LDRi(decoder_2_out7[24]), .T(or_1_out), .out_7(a3_out_7),
    .OutPut(Zero_output), .Reset(Reset), .Write(RegWrite));
  Decoder #(.select(5), .enable("false")) decoder_1 (
    .out0(decoder_1_out31[31]), .out1(decoder_1_out31[30]), .out2(decoder_1_out31[29]),
    .out3(decoder_1_out31[28]), .out4(decoder_1_out31[27]), .out5(decoder_1_out31[26]),
    .out6(decoder_1_out31[25]), .out7(decoder_1_out31[24]), .out8(decoder_1_out31[23]),
    .out9(decoder_1_out31[22]), .out10(decoder_1_out31[21]), .out11(decoder_1_out31[20]),
    .out12(decoder_1_out31[19]), .out13(decoder_1_out31[18]), .out14(decoder_1_out31[17]),
    .out15(decoder_1_out31[16]), .out16(decoder_1_out31[15]), .out17(decoder_1_out31[14]),
    .out18(decoder_1_out31[13]), .out19(decoder_1_out31[12]), .out20(decoder_1_out31[11]),
    .out21(decoder_1_out31[10]), .out22(decoder_1_out31[9]), .out23(decoder_1_out31[8]),
    .out24(decoder_1_out31[7]), .out25(decoder_1_out31[6]), .out26(decoder_1_out31[5]),
    .out27(decoder_1_out31[4]), .out28(decoder_1_out31[3]), .out29(decoder_1_out31[2]),
    .out30(decoder_1_out31[1]), .out31(decoder_1_out31[0]), .sel(multiplexer_1_out));
  // Probe on t0_out_7
  // Probe on t1_out_7
  // Probe on t2_out_7
  // Probe on t3_out_7
  // Probe on t4_out_7
  // Probe on t5_out_7
  // Probe on t6_out_7
  // Probe on t7_out_7
  Ri u_t0 (
    .Input(WriteData), .Ri_B(decoder_1_out31[23]), .LDRi(decoder_2_out15[7]), .T(or_1_out), .out_7(t0_out_7),
    .OutPut(Zero_output), .Reset(Reset), .Write(RegWrite));
  Ri u_t1 (
    .Input(WriteData), .Ri_B(decoder_1_out31[22]), .LDRi(decoder_2_out15[6]), .T(or_1_out), .out_7(t1_out_7),
    .OutPut(Zero_output), .Reset(Reset), .Write(RegWrite));
  Ri t2 (
    .Input(WriteData), .Ri_B(decoder_1_out31[21]), .LDRi(decoder_2_out15[5]), .T(or_1_out), .out_7(t2_out_7),
    .OutPut(Zero_output), .Reset(Reset), .Write(RegWrite));
  Ri t3 (
    .Input(WriteData), .Ri_B(decoder_1_out31[20]), .LDRi(decoder_2_out15[4]), .T(or_1_out), .out_7(t3_out_7),
    .OutPut(Zero_output), .Reset(Reset), .Write(RegWrite));
  Ri t4 (
    .Input(WriteData), .Ri_B(decoder_1_out31[19]), .LDRi(decoder_2_out15[3]), .T(or_1_out), .out_7(t4_out_7),
    .OutPut(Zero_output), .Reset(Reset), .Write(RegWrite));
  Ri t5 (
    .Input(WriteData), .Ri_B(decoder_1_out31[18]), .LDRi(decoder_2_out15[2]), .T(or_1_out), .out_7(t5_out_7),
    .OutPut(Zero_output), .Reset(Reset), .Write(RegWrite));
  Ri t6 (
    .Input(WriteData), .Ri_B(decoder_1_out31[17]), .LDRi(decoder_2_out15[1]), .T(or_1_out), .out_7(t6_out_7),
    .OutPut(Zero_output), .Reset(Reset), .Write(RegWrite));
  Ri t7 (
    .Input(WriteData), .Ri_B(decoder_1_out31[16]), .LDRi(decoder_2_out15[0]), .T(or_1_out), .out_7(t7_out_7),
    .OutPut(Zero_output), .Reset(Reset), .Write(RegWrite));
  // Probe on s0_out_7
  // Probe on s1_out_7
  // Probe on s2_out_7
  // Probe on s3_out_7
  // Probe on s4_out_7
  // Probe on s5_out_7
  // Probe on s6_out_7
  // Probe on s7_out_7
  Ri s0 (
    .Input(WriteData), .Ri_B(decoder_1_out31[15]), .LDRi(decoder_2_out23[7]), .T(or_1_out), .out_7(s0_out_7),
    .OutPut(Zero_output), .Reset(Reset), .Write(RegWrite));
  Ri s1 (
    .Input(WriteData), .Ri_B(decoder_1_out31[14]), .LDRi(decoder_2_out23[6]), .T(or_1_out), .out_7(s1_out_7),
    .OutPut(Zero_output), .Reset(Reset), .Write(RegWrite));
  Ri s2 (
    .Input(WriteData), .Ri_B(decoder_1_out31[13]), .LDRi(decoder_2_out23[5]), .T(or_1_out), .out_7(s2_out_7),
    .OutPut(Zero_output), .Reset(Reset), .Write(RegWrite));
  Ri s3 (
    .Input(WriteData), .Ri_B(decoder_1_out31[12]), .LDRi(decoder_2_out23[4]), .T(or_1_out), .out_7(s3_out_7),
    .OutPut(Zero_output), .Reset(Reset), .Write(RegWrite));
  Ri s4 (
    .Input(WriteData), .Ri_B(decoder_1_out31[11]), .LDRi(decoder_2_out23[3]), .T(or_1_out), .out_7(s4_out_7),
    .OutPut(Zero_output), .Reset(Reset), .Write(RegWrite));
  Ri s5 (
    .Input(WriteData), .Ri_B(decoder_1_out31[10]), .LDRi(decoder_2_out23[2]), .T(or_1_out), .out_7(s5_out_7),
    .OutPut(Zero_output), .Reset(Reset), .Write(RegWrite));
  Ri s6 (
    .Input(WriteData), .Ri_B(decoder_1_out31[9]), .LDRi(decoder_2_out23[1]), .T(or_1_out), .out_7(s6_out_7),
    .OutPut(Zero_output), .Reset(Reset), .Write(RegWrite));
  Ri s7 (
    .Input(WriteData), .Ri_B(decoder_1_out31[8]), .LDRi(decoder_2_out23[0]), .T(or_1_out), .out_7(s7_out_7),
    .OutPut(Zero_output), .Reset(Reset), .Write(RegWrite));
  // Probe on t8_out_7
  // Probe on t9_out_7
  // Probe on k0_out_7
  // Probe on k1_out_7
  // Probe on gp_out_7
  // Probe on sp_out_7
  // Probe on fp_out_7
  // Probe on ra_out_7
  Ri t8 (
    .Input(WriteData), .Ri_B(decoder_1_out31[7]), .LDRi(decoder_2_out31[7]), .T(or_1_out), .out_7(t8_out_7),
    .OutPut(Zero_output), .Reset(Reset), .Write(RegWrite));
  Ri t9 (
    .Input(WriteData), .Ri_B(decoder_1_out31[6]), .LDRi(decoder_2_out31[6]), .T(or_1_out), .out_7(t9_out_7),
    .OutPut(Zero_output), .Reset(Reset), .Write(RegWrite));
  Ri k0 (
    .Input(WriteData), .Ri_B(decoder_1_out31[5]), .LDRi(decoder_2_out31[5]), .T(or_1_out), .out_7(k0_out_7),
    .OutPut(Zero_output), .Reset(Reset), .Write(RegWrite));
  Ri k1 (
    .Input(WriteData), .Ri_B(decoder_1_out31[4]), .LDRi(decoder_2_out31[4]), .T(or_1_out), .out_7(k1_out_7),
    .OutPut(Zero_output), .Reset(Reset), .Write(RegWrite));
  Ri gp (
    .Input(WriteData), .Ri_B(decoder_1_out31[3]), .LDRi(decoder_2_out31[3]), .T(or_1_out), .out_7(gp_out_7),
    .OutPut(Zero_output), .Reset(Reset), .Write(RegWrite));
  Ri sp (
    .Input(WriteData), .Ri_B(decoder_1_out31[2]), .LDRi(decoder_2_out31[2]), .T(or_1_out), .out_7(sp_out_7),
    .OutPut(Zero_output), .Reset(Reset), .Write(RegWrite));
  Ri fp (
    .Input(WriteData), .Ri_B(decoder_1_out31[1]), .LDRi(decoder_2_out31[1]), .T(or_1_out), .out_7(fp_out_7),
    .OutPut(Zero_output), .Reset(Reset), .Write(RegWrite));
  Ri ra (
    .Input(WriteData), .Ri_B(decoder_1_out31[0]), .LDRi(decoder_2_out31[0]), .T(or_1_out), .out_7(ra_out_7),
    .OutPut(Zero_output), .Reset(Reset), .Write(RegWrite));
  Demultiplexer #(.width(32), .enable("false")) demultiplexer_1 (
    .out0(Output0), .out1(OutPut1), .in(Zero_output), .sel(and_1_out));
  Decoder #(.select(5), .enable("false")) decoder_2 (
    .out0(decoder_2_out7[31]), .out1(decoder_2_out7[30]), .out2(decoder_2_out7[29]),
    .out3(decoder_2_out7[28]), .out4(decoder_2_out7[27]), .out5(decoder_2_out7[26]),
    .out6(decoder_2_out7[25]), .out7(decoder_2_out7[24]), .out8(decoder_2_out15[7]),
    .out9(decoder_2_out15[6]), .out10(decoder_2_out15[5]), .out11(decoder_2_out15[4]),
    .out12(decoder_2_out15[3]), .out13(decoder_2_out15[2]), .out14(decoder_2_out15[1]),
    .out15(decoder_2_out15[0]), .out16(decoder_2_out23[7]), .out17(decoder_2_out23[6]),
    .out18(decoder_2_out23[5]), .out19(decoder_2_out23[4]), .out20(decoder_2_out23[3]),
    .out21(decoder_2_out23[2]), .out22(decoder_2_out23[1]), .out23(decoder_2_out23[0]),
    .out24(decoder_2_out31[7]), .out25(decoder_2_out31[6]), .out26(decoder_2_out31[5]),
    .out27(decoder_2_out31[4]), .out28(decoder_2_out31[3]), .out29(decoder_2_out31[2]),
    .out30(decoder_2_out31[1]), .out31(decoder_2_out31[0]), .sel(WriteReg));

  // Notes on the sheet:
  //   0
  //   1
  //   2
  //   3
  //   4
  //   5
  //   6
  //   7
  //   8
  //   9
  //   10
  //   11
  //   12
  //   13
  //   14
  //   15
  //   16
  //   17
  //   18
  //   19
  //   20
  //   21
  //   22
  //   23
  //   24
  //   25
  //   26
  //   27
  //   28
  //   29
  //   30
  //   31
endmodule

module Ri (
  input  [31:0] Input,
  input  Write,
  input  Ri_B,
  input  LDRi,
  input  T,
  input  Reset,
  output [31:0] out_7,
  output [31:0] OutPut
);

  wire and_1_out;

  and and_1 (and_1_out, Write, LDRi);
  Register #(.width(32)) register_1 (.D(Input), .en(and_1_out), .Q(out_7), .clk(T), .clr(Reset));
  assign OutPut = Ri_B ? out_7 : 32'bz;  // Controlled_Buffer controlled_buffer_1
endmodule

module ID_EX (
  input  [1:0] WB,
  input  [2:0] M,
  input  [5:0] EX,
  input  [31:0] C_PC_4,
  input  [31:0] Fatch1,
  input  [31:0] Fatch2,
  input  [31:0] _15_0_signEx,
  input  [4:0] _26_21_rs,
  input  [4:0] _20_16_rt,
  input  [4:0] _15_11_rd,
  input  T1,
  input  T0,
  input  reset,
  output [1:0] WB_out,
  output [2:0] M_out,
  output RegDst,
  output [3:0] ALUOp4,
  output ALUSrc,
  output [31:0] C_PC_4_out,
  output [31:0] Fatch1_out,
  output [31:0] Fatch2_out,
  output [31:0] _15_0_signEx_out,
  output [4:0] _26_21_rs_out,
  output [4:0] _20_16_rt_out,
  output [4:0] _15_11_rd_out
);

  wire and_1_out, and_2_out, not_1_out, not_2_out;

  not not_1 (not_1_out, T1);
  and and_1 (and_1_out, not_1_out, T0);
  and and_2 (and_2_out, T1, not_2_out);
  not not_2 (not_2_out, T0);
  Register #(.width(2)) register_1 (.D(WB), .en(1'b1), .Q(WB_out), .clk(and_2_out), .clr(reset));
  Register #(.width(3)) register_2 (.D(M), .en(1'b1), .Q(M_out), .clk(and_2_out), .clr(reset));
  Register #(.width(6)) register_3 (.D(EX), .en(1'b1), .Q({RegDst, ALUOp4, ALUSrc}), .clk(and_2_out), .clr(reset));
  Register #(.width(32)) register_4 (.D(C_PC_4), .en(1'b1), .Q(C_PC_4_out), .clk(and_2_out), .clr(reset));
  Register #(.width(32)) register_5 (.D(Fatch2), .en(1'b1), .Q(Fatch2_out), .clk(and_2_out), .clr(reset));
  Register #(.width(32)) register_6 (.D(_15_0_signEx), .en(1'b1), .Q(_15_0_signEx_out), .clk(and_2_out), .clr(reset));
  Register #(.width(5)) register_7 (.D(_26_21_rs), .en(1'b1), .Q(_26_21_rs_out), .clk(and_2_out), .clr(reset));
  Register #(.width(5)) register_8 (.D(_20_16_rt), .en(1'b1), .Q(_20_16_rt_out), .clk(and_2_out), .clr(reset));
  Register #(.width(5)) register_9 (.D(_15_11_rd), .en(1'b1), .Q(_15_11_rd_out), .clk(and_2_out), .clr(reset));
  Register #(.width(32)) register_10 (.D(Fatch1), .en(1'b1), .Q(Fatch1_out), .clk(and_1_out), .clr(reset));
endmodule

module signExtend (
  input  [15:0] In,
  output [31:0] Out
);

  assign Out = {{16{In[15]}}, In};  // Bit_Extender bit_extender_1
endmodule

module left_shift (
  input  [31:0] Input,
  input  [4:0] distance,
  output [31:0] Out
);

  wire [4:0] undriven;

  Shifter #(.width(32)) shifter_1 (.\dist (undriven));  // open: in, out

  assign Out = Input;
endmodule

module EX_MEM (
  input  [1:0] WB,
  input  [2:0] M,
  input  [31:0] New_PC,
  input  Zero,
  input  [31:0] ALU_result,
  input  [31:0] Fatch_2,
  input  [4:0] _5_rd,
  input  clk,
  input  reset,
  output [1:0] WB_output,
  output MemWrite,
  output MemRead,
  output Branch,
  output [31:0] new_PC_out,
  output Zero_out,
  output [31:0] ALU_result_out,
  output [31:0] Fatch_2_out,
  output [4:0] _5_rd_out
);

  Register #(.width(2)) register_1 (.D(WB), .en(1'b1), .Q(WB_output), .clk(clk), .clr(reset));
  Register #(.width(3)) register_2 (.D(M), .en(1'b1), .Q({Branch, MemRead, MemWrite}), .clk(clk), .clr(reset));
  Register #(.width(32)) register_3 (.D(New_PC), .en(1'b1), .Q(new_PC_out), .clk(clk), .clr(reset));
  Register #(.width(1)) register_4 (.D(Zero), .en(1'b1), .Q(Zero_out), .clk(clk), .clr(reset));
  Register #(.width(32)) register_5 (.D(ALU_result), .en(1'b1), .Q(ALU_result_out), .clk(clk), .clr(reset));
  Register #(.width(32)) register_6 (.D(Fatch_2), .en(1'b1), .Q(Fatch_2_out), .clk(clk), .clr(reset));
  Register #(.width(5)) register_7 (.D(_5_rd), .en(1'b1), .Q(_5_rd_out), .clk(clk), .clr(reset));
endmodule

module MEM_WB (
  input  [1:0] WB,
  input  [31:0] mem_data,
  input  [31:0] ALU_result,
  input  [4:0] _5_rd,
  input  clk,
  input  reset,
  output MemToReg,
  output RegWrite,
  output [31:0] mem_read_out,
  output [31:0] ALU_result_out,
  output [4:0] _5_rd_result
);

  Register #(.width(2)) register_1 (.D(WB), .en(1'b1), .Q({RegWrite, MemToReg}), .clk(clk), .clr(reset));
  Register #(.width(32)) register_2 (.D(mem_data), .en(1'b1), .Q(mem_read_out), .clk(clk), .clr(reset));
  Register #(.width(32)) register_3 (.D(ALU_result), .en(1'b1), .Q(ALU_result_out), .clk(clk), .clr(reset));
  Register #(.width(5)) register_4 (.D(_5_rd), .en(1'b1), .Q(_5_rd_result), .clk(clk), .clr(reset));
endmodule

module Controler (
  input  [5:0] Opcode,
  input  [5:0] funct,
  output [5:0] Ex_out,
  output [2:0] M_out,
  output [1:0] WB_out
);

  wire and_2_out, and_3_out, and_7_out, and_8_out, not_1_out, not_2_out, not_3_out;

  not not_1 (not_1_out, Opcode[2]);
  not not_2 (not_2_out, Opcode[3]);
  not not_3 (not_3_out, Opcode[5]);
  and and_1 (Ex_out[5], not_1_out, not_3_out);
  and and_2 (and_2_out, not_1_out, not_3_out);
  and and_3 (and_3_out, not_3_out, Opcode[2]);
  and and_4 (M_out[2], Opcode[2], not_3_out);
  and and_5 (M_out[1], Opcode[5], not_2_out);
  and and_6 (M_out[0], Opcode[3], Opcode[5]);
  and and_7 (and_7_out, not_3_out, not_1_out);
  and and_8 (and_8_out, Opcode[5], not_2_out);
  and and_9 (WB_out[0], Opcode[5], not_2_out);
  or or_1 (WB_out[1], and_7_out, and_8_out);
  ALUControler alucontroler_1 (.ALUOp1(and_2_out), .ALUOp0(and_3_out), .Funct(funct), .ALU_Control_signal(Ex_out[4:1]));

  assign Ex_out[0] = Opcode[5];

  // Notes on the sheet:
  //   RegDst
  //   ALUOp1
  //   ALUOp0
  //   ALUSrc
  //   Branch
  //   MemRead
  //   MemWrite
  //   RegWrite
  //   MemToReg
endmodule

module ALUControler (
  input  ALUOp1,
  input  ALUOp0,
  input  [5:0] Funct,
  output [3:0] ALU_Control_signal
);

  wire and_1_out, and_2_out, and_3_out, and_4_out, and_5_out, and_6_out, not_1_out, not_2_out, not_3_out,
       not_4_out, not_5_out, not_6_out, not_7_out;

  not not_1 (not_1_out, Funct[0]);
  not not_2 (not_2_out, ALUOp1);
  not not_3 (not_3_out, ALUOp0);
  not not_4 (not_4_out, Funct[1]);
  not not_5 (not_5_out, Funct[2]);
  not not_6 (not_6_out, Funct[3]);
  not not_7 (not_7_out, Funct[4]);
  and and_1 (and_1_out, not_2_out, ALUOp0);
  and and_2 (and_2_out, ALUOp1, not_3_out, Funct[5], not_7_out, not_5_out, Funct[1], not_1_out);
  and and_3 (and_3_out, ALUOp1, not_3_out, Funct[5], not_7_out, not_5_out, not_1_out);
  and and_4 (and_4_out, ALUOp1, not_3_out, Funct[5], not_7_out, Funct[3], not_5_out, Funct[1], not_1_out);
  and and_5 (and_5_out, ALUOp1, not_3_out, Funct[5], not_7_out, not_6_out, Funct[2], not_4_out, Funct[0]);
  and and_6 (and_6_out, ALUOp1, not_3_out, Funct[5], not_7_out, Funct[3], not_5_out, Funct[1], not_1_out);
  or or_1 (ALU_Control_signal[2], and_1_out, and_2_out);
  or or_2 (ALU_Control_signal[1], not_2_out, and_3_out, and_4_out);
  or or_3 (ALU_Control_signal[0], and_5_out, and_6_out);

  assign ALU_Control_signal[3] = 1'b0;
endmodule

module ClockGen (
  input  \单节拍按钮 ,
  input  \主频 ,
  input  \单周期按钮 ,
  input  \单拍0_单周期1 ,
  input  \连续运行1 ,
  output T4,
  output T3,
  output T2,
  output T1
);

  wire controlled_buffer_1_out, controlled_buffer_2_out, controlled_buffer_3_out, counter_1_q, not_1_out,
       not_2_out, xor_1_out;
  wire [1:0] counter_2_q;

  Counter #(.width(1), .max('h1)) counter_1 (
    .load(1'b0), .count(1'b1), .Q(counter_1_q), .clk(xor_1_out));  // open: D, carry, clr
  xor xor_1 (xor_1_out, \单周期按钮 , T4);
  assign controlled_buffer_1_out = not_1_out ? \单节拍按钮  : 1'bz;  // Controlled_Buffer controlled_buffer_1
  assign controlled_buffer_2_out = counter_1_q ? \主频  : 1'bz;  // Controlled_Buffer controlled_buffer_2
  not not_1 (not_1_out, \单拍0_单周期1 );
  Counter #(.width(2), .max('h3)) counter_2 (
    .load(1'b0), .count(1'b1), .Q(counter_2_q), .clk(controlled_buffer_3_out));  // open: D, carry, clr
  assign controlled_buffer_3_out = \连续运行1  ? \主频  : 1'bz;  // Controlled_Buffer controlled_buffer_3
  assign controlled_buffer_3_out = not_2_out ? controlled_buffer_1_out : 1'bz;  // Controlled_Buffer controlled_buffer_4
  assign controlled_buffer_1_out = \单拍0_单周期1  ? controlled_buffer_2_out : 1'bz;  // Controlled_Buffer controlled_buffer_5
  not not_2 (not_2_out, \连续运行1 );
  Demultiplexer #(.select(2)) demultiplexer_1 (
    .out0(T1), .out1(T2), .out2(T3), .out3(T4), .in(1'b1), .sel(counter_2_q), .en(1'b1));
endmodule

module ForwardingUnit (
  input  [4:0] EX_MEM_Rd,
  input  [4:0] ID_EX_Rs,
  input  [4:0] ID_EX_Rt,
  input  [4:0] MEM_WB_Rd,
  input  EX_MEM_M_RegWrite,
  input  MEM_WB_M_RegWrite,
  output [1:0] ForwardA,
  output [1:0] ForwardB
);

  wire and_2_out, and_3_out, and_5_out, and_6_out, comparator_1_eq, comparator_2_eq, comparator_3_eq,
       comparator_4_eq, comparator_5_eq, comparator_6_eq, not_1_out, not_2_out, not_3_out, not_4_out;

  not not_1 (not_1_out, EX_MEM_M_RegWrite);
  Comparator #(.width(5)) comparator_1 (.a(EX_MEM_Rd), .b({5{1'b0}}), .eq(comparator_1_eq));  // open: gt, lt
  not not_2 (not_2_out, comparator_2_eq);
  Comparator #(.width(5)) comparator_2 (.a(EX_MEM_Rd), .b(ID_EX_Rs), .eq(comparator_2_eq));  // open: gt, lt
  not not_3 (not_3_out, comparator_3_eq);
  Comparator #(.width(5)) comparator_3 (.a(EX_MEM_Rd), .b(ID_EX_Rt), .eq(comparator_3_eq));  // open: gt, lt
  Comparator #(.width(5)) comparator_4 (.a(ID_EX_Rt), .b(MEM_WB_Rd), .eq(comparator_4_eq));  // open: gt, lt
  Comparator #(.width(5)) comparator_5 (.a(MEM_WB_Rd), .b({5{1'b0}}), .eq(comparator_5_eq));  // open: gt, lt
  Comparator #(.width(5)) comparator_6 (.a(ID_EX_Rs), .b(MEM_WB_Rd), .eq(comparator_6_eq));  // open: gt, lt
  not not_4 (not_4_out, comparator_1_eq);
  and and_1 (ForwardA[1], comparator_2_eq, not_4_out, EX_MEM_M_RegWrite);
  and and_2 (and_2_out, not_2_out, comparator_5_eq, comparator_6_eq, not_1_out, MEM_WB_M_RegWrite);
  and and_3 (and_3_out, comparator_1_eq, not_2_out, comparator_6_eq, comparator_5_eq, MEM_WB_M_RegWrite);
  and and_4 (ForwardB[1], not_4_out, EX_MEM_M_RegWrite, comparator_3_eq);
  and and_5 (and_5_out, not_3_out, comparator_5_eq, comparator_4_eq, not_1_out, MEM_WB_M_RegWrite);
  and and_6 (and_6_out, comparator_1_eq, not_3_out, comparator_5_eq, comparator_4_eq, MEM_WB_M_RegWrite);
  or or_1 (ForwardA[0], and_2_out, and_3_out);
  or or_2 (ForwardB[0], and_5_out, and_6_out);
endmodule
